# Fritzing sketch prototype_setup (saved by Fritzing 0.9.10b)
breadboards: 1

parts:
  Part1 = Adafruit Feather M4 Express CAN
  RE1 = KY-040 Rotary encoder [package=THT]
  NEOPIXEL1 = Neopixel Strip -- Black (60/m) [part_number=1461]
  Power_plug1 = Power plug
  LCD1 = LCD screen
  LCM1602_IIC1 = LCM1602 IIC [part_number="LCM1602 IIC" chip_label="LCM1602 IIC" package="DIP (Dual Inline) [THT]"]

nets:
  GND: Part1.GND, RE1.GND, NEOPIXEL1.GND, Power_plug1.GND, LCM1602_IIC1.GND
  VCC: Part1.+3V3, RE1.Vcc, LCM1602_IIC1.VCC
  N1: Part1.D13, NEOPIXEL1.DI
  N2: Part1.D9, RE1.SW
  N3: Part1.D6, RE1.CLK
  N4: Part1.D5, RE1.DT
  N5: Part1.SCL, LCM1602_IIC1.SCL
  N6: Part1.SDA, LCM1602_IIC1.SDA
  +5V: NEOPIXEL1.+5V, Power_plug1.VCC
  VSS: LCD1.VSS, LCM1602_IIC1.VSS
  VDD: LCD1.VDD, LCM1602_IIC1.VDD
  N7: LCD1.V0, LCM1602_IIC1.V0
  N8: LCD1.RS, LCM1602_IIC1.RS
  N9: LCD1.R/W, LCM1602_IIC1.RW
  N10: LCD1.E, LCM1602_IIC1.E
  N11: LCD1.DB0, LCM1602_IIC1.D0
  N12: LCD1.DB1, LCM1602_IIC1.D1
  N13: LCD1.DB2, LCM1602_IIC1.D2
  N14: LCD1.DB3, LCM1602_IIC1.D3
  N15: LCD1.DB4, LCM1602_IIC1.D4
  N16: LCD1.DB5, LCM1602_IIC1.D5
  N17: LCD1.DB6, LCM1602_IIC1.D6
  N18: LCD1.DB7, LCM1602_IIC1.D7
  N19: LCD1.LED+, LCM1602_IIC1.A
  N20: LCD1.LED-, LCM1602_IIC1.K

custom parts:
  KY-040 Rotary encoder: KY-040 Rotary Encoder with switch on breakout borad from AZ Delivery
  Neopixel Strip -- Black (60/m): Neopixel Strip, Black, 60 pixels per meter.
  LCM1602 IIC: I2C-Module to use a 1602 or 2004 LCD on with the wire.h libory Serial LCD Modul
